// Logisim project Game.circ as structural Verilog
module main (
  input  in_1
);

  wire ResetBar_out;
  wire [31:0] barhandler_1_output;

  Button L (.out(in_1));
  BarHandler barhandler_1 (.reset(ResetBar_out), .R(in_1), .L(in_1), .\output (barhandler_1_output));
  Button ResetBar (.out(ResetBar_out));
  DotMatrix #(.inputtype("row"), .matrixcols(32), .matrixrows(32), .dotshape("circle")) dotmatrix_1 (.row31(barhandler_1_output));  // open: row0, row1, row2, row3, row4, row5, row6, row7, row8, row9, row10, row11, row12, row13, row14, row15, row16, row17, row18, row19, row20, row21, row22, row23, row24, row25, row26, row27, row28, row29, row30
  // Probe on barhandler_1_output
endmodule

module BarHandler (
  input  reset,
  input  R,
  input  L,
  output [31:0] \output 
);

  wire clock, L_t, Left, R_t, Reset_t, reset_t_t, Right, update;
  wire [31:0] divider_1_out, multiplexer_1_out, multiplexer_2_out, multiplier_1_out, register_1_q;

  Clock clock_1 (.out(clock));
  or or_1 (R_t, R, Right);
  or or_2 (L_t, L, Left);
  or or_3 (reset_t_t, reset, Reset_t);
  or or_4 (update, R_t, L_t, reset_t_t);
  Multiplexer #(.width(32)) multiplexer_1 (
    .in0(\output ), .in1(32'h38000), .out(multiplexer_1_out), .sel(reset_t_t));  // open: en
  Register #(.width(32)) register_1 (.D(multiplexer_1_out), .en(update), .Q(register_1_q), .clk(clock));  // open: clr
  DotMatrix #(.inputtype("row"), .matrixcols(32), .matrixrows(2)) dotmatrix_1 (.row1(\output ));  // open: row0
  // Probe on register_1_q
  Button button_1 (.out(Right));
  Multiplier #(.width(32)) multiplier_1 (.a(register_1_q), .b(32'h2), .out(multiplier_1_out));  // open: cin, cout
  Divider #(.width(32)) divider_1 (.a(register_1_q), .b(32'h2), .out(divider_1_out));  // open: upper, rem
  Button button_2 (.out(Left));
  Button button_3 (.out(Reset_t));
  Multiplexer #(.width(32)) multiplexer_2 (
    .in0(multiplier_1_out), .in1(divider_1_out), .out(multiplexer_2_out), .sel(R_t));  // open: en
  ColisionHandler colisionhandler_1 (.Entrada_sin_depurar(multiplexer_2_out), .Salida_depurada(\output ));

  // Other names for the same wires on the sheet: out[31:0] = \output 
endmodule

module ColisionHandler (
  input  [31:0] Entrada_sin_depurar,
  output [31:0] Salida_depurada
);

  wire comparator_1_eq, comparator_2_eq, comparator_3_eq, comparator_4_eq, comparator_5_eq, comparator_6_eq;
  wire [1:0] multiplexer_6_out, varcolision, varcolision1, varcolision2;
  wire [31:0] sal1, sal2;

  Comparator #(.width(32)) comparator_1 (
    .a(Entrada_sin_depurar), .b(32'h80000000), .eq(comparator_1_eq));  // open: gt, lt
  Comparator #(.width(32)) comparator_2 (.a(Entrada_sin_depurar), .b(32'h1), .eq(comparator_2_eq));  // open: gt, lt
  Multiplexer #(.width(32)) multiplexer_1 (
    .in0(Entrada_sin_depurar), .in1(32'h7), .out(sal1), .sel(comparator_1_eq));  // open: en
  Multiplexer #(.width(32)) multiplexer_2 (
    .in0(Entrada_sin_depurar), .in1(32'he0000000), .out(sal2), .sel(comparator_2_eq));  // open: en
  Comparator #(.width(32)) comparator_3 (.a(Entrada_sin_depurar), .b(sal1), .eq(comparator_3_eq));  // open: gt, lt
  Comparator #(.width(32)) comparator_4 (.a(Entrada_sin_depurar), .b(sal2), .eq(comparator_4_eq));  // open: gt, lt
  Multiplexer #(.width(2)) multiplexer_3 (
    .in0(2'b00), .in1(2'b10), .out(varcolision1), .sel(comparator_3_eq));  // open: en
  Multiplexer #(.width(2)) multiplexer_4 (
    .in0(2'b01), .in1(2'b10), .out(varcolision2), .sel(comparator_4_eq));  // open: en
  Multiplexer #(.select(2), .width(32)) multiplexer_5 (
    .in0(sal1), .in1(sal2), .in3(Entrada_sin_depurar), .out(Salida_depurada), .sel(varcolision));  // open: in2, en
  Multiplexer #(.width(2)) multiplexer_6 (
    .in0(varcolision2), .in1(varcolision1), .out(multiplexer_6_out), .sel(comparator_5_eq));  // open: en
  Comparator #(.width(2)) comparator_5 (.a(varcolision1), .b(2'b00), .eq(comparator_5_eq));  // open: gt, lt
  Comparator #(.width(2)) comparator_6 (.a(varcolision1), .b(varcolision2), .eq(comparator_6_eq));  // open: gt, lt
  Multiplexer #(.width(2)) multiplexer_7 (
    .in0(multiplexer_6_out), .in1(2'b11), .out(varcolision), .sel(comparator_6_eq));  // open: en

  // Other names for the same wires on the sheet: colisioninput[31:0] = Entrada_sin_depurar
endmodule

module AsteroidController (
);

  wire clock_1_out, t_ff_1_q, t_ff_2_q;
  wire [31:0] and_1_out, random_1_out, random_2_out, random_3_out, random_4_out, random_5_out, random_6_out;

  Clock clock_1 (.out(clock_1_out));
  T_Flip_Flop t_ff_1 (.clk(clock_1_out), .T(clock_1_out), .Q(t_ff_1_q));  // open: Qn, preset, reset, en
  T_Flip_Flop t_ff_2 (.clk(t_ff_1_q), .T(t_ff_1_q), .Q(t_ff_2_q));  // open: Qn, preset, reset, en
  Random #(.width(32)) random_1 (.clk(t_ff_2_q), .out(random_1_out));  // open: next, clr
  Random #(.width(32)) random_2 (.clk(t_ff_2_q), .out(random_2_out));  // open: next, clr
  Random #(.width(32)) random_3 (.clk(t_ff_2_q), .out(random_3_out));  // open: next, clr
  Random #(.width(32)) random_4 (.clk(t_ff_2_q), .out(random_4_out));  // open: next, clr
  Random #(.width(32)) random_5 (.clk(t_ff_2_q), .out(random_5_out));  // open: next, clr
  Random #(.width(32)) random_6 (.clk(t_ff_2_q), .out(random_6_out));  // open: next, clr
  // Probe on and_1_out
  assign and_1_out = random_1_out & random_2_out & random_3_out & random_4_out & random_5_out & random_6_out;  // AND_Gate and_1, 32 bits wide
  DotMatrix #(.inputtype("row"), .matrixcols(32), .matrixrows(2)) dotmatrix_1 (.row0(and_1_out));  // open: row1
endmodule
